// Logisim project FS.circ as structural Verilog: 1 circuit, main circuit main
module main (
  input  A,
  input  B,
  input  Cin,
  output differece,
  output carry
);

  wire and_1_out, and_2_out, and_3_out, not_1_out, xor_1_out;

  not not_1 (not_1_out, A);
  xor xor_1 (xor_1_out, A, B);
  and and_1 (and_1_out, not_1_out, B);
  and and_2 (and_2_out, B, Cin);
  and and_3 (and_3_out, not_1_out, Cin);
  xor xor_2 (differece, xor_1_out, Cin);
  or or_1 (carry, and_1_out, and_2_out, and_3_out);
endmodule
