// Logisim project HS.circ as structural Verilog: 1 circuit, main circuit main
module main (
  input  A,
  input  B,
  output differece,
  output carry
);

  wire not_1_out;

  not not_1 (not_1_out, A);
  xor xor_1 (differece, A, B);
  and and_1 (carry, not_1_out, B);
endmodule
