// Logisim project subtacter(6-bit).circ as structural Verilog: 1 circuit, main circuit main
module main (
  input  A5,
  input  A4,
  input  A3,
  input  A2,
  input  A1,
  input  A0,
  input  B5,
  input  B4,
  input  B3,
  input  B2,
  input  B1,
  input  B0,
  output Carry,
  output S5,
  output S4,
  output S3,
  output S2,
  output S1,
  output S0
);

  wire main_2_carry, main_3_carry, main_4_carry, main_5_carry, main_6_carry;

  FS_main main_1 (.A(A5), .B(B5), .Cin(main_2_carry), .differece(S5), .carry(Carry));
  FS_main main_2 (.A(A4), .B(B4), .Cin(main_3_carry), .differece(S4), .carry(main_2_carry));
  FS_main main_3 (.A(A3), .B(B3), .Cin(main_4_carry), .differece(S3), .carry(main_3_carry));
  FS_main main_4 (.A(A2), .B(B2), .Cin(main_5_carry), .differece(S2), .carry(main_4_carry));
  FS_main main_5 (.A(A1), .B(B1), .Cin(main_6_carry), .differece(S1), .carry(main_5_carry));
  HS_main main_6 (.A(A0), .B(B0), .differece(S0), .carry(main_6_carry));
endmodule
