// Logisim project subtacter(6-bit)[using full adder].circ as structural Verilog: 1 circuit, main circuit main
module main (
  input  A5,
  input  A4,
  input  A3,
  input  A2,
  input  A1,
  input  A0,
  input  B5,
  input  B4,
  input  B3,
  input  B2,
  input  B1,
  input  B0,
  output Carry,
  output S5,
  output S4,
  output S3,
  output S2,
  output S1,
  output S0
);

  wire main_2_carry, main_3_carry, main_4_carry, main_5_carry, main_6_carry, not_1_out, not_2_out, not_3_out,
       not_4_out, not_5_out, not_6_out;

  not not_1 (not_1_out, B5);
  FA_main main_1 (.A(A5), .B(not_1_out), .Cin(main_2_carry), .sum(S5), .carry(Carry));
  not not_2 (not_2_out, B4);
  FA_main main_2 (.A(A4), .B(not_2_out), .Cin(main_3_carry), .sum(S4), .carry(main_2_carry));
  not not_3 (not_3_out, B3);
  FA_main main_3 (.A(A3), .B(not_3_out), .Cin(main_4_carry), .sum(S3), .carry(main_3_carry));
  not not_4 (not_4_out, B2);
  FA_main main_4 (.A(A2), .B(not_4_out), .Cin(main_5_carry), .sum(S2), .carry(main_4_carry));
  not not_5 (not_5_out, B1);
  FA_main main_5 (.A(A1), .B(not_5_out), .Cin(main_6_carry), .sum(S1), .carry(main_5_carry));
  not not_6 (not_6_out, B0);
  FA_main main_6 (.A(A0), .B(not_6_out), .Cin(1'b1), .sum(S0), .carry(main_6_carry));
endmodule
