// Logisim project 8-bit register.circ as structural Verilog: 1 circuit, main circuit main
module main (
  input  Input,
  input  CLK,
  input  Preset,
  input  Enable,
  input  Reset,
  output R7,
  output R6,
  output R5,
  output R4,
  output R3,
  output R2,
  output R1,
  output R0
);

  wire j_k_ff_1_qn, j_k_ff_2_qn, j_k_ff_3_qn, j_k_ff_4_qn, j_k_ff_5_qn, j_k_ff_6_qn, j_k_ff_7_qn, not_1_out;

  not not_1 (not_1_out, Input);
  J_K_Flip_Flop j_k_ff_1 (
    .J(Input), .clk(CLK), .K(not_1_out), .Q(R7), .Qn(j_k_ff_1_qn), .preset(Preset), .en(Enable), .reset(Reset));
  J_K_Flip_Flop j_k_ff_2 (
    .J(R7), .clk(CLK), .K(j_k_ff_1_qn), .Q(R6), .Qn(j_k_ff_2_qn), .preset(Preset), .en(Enable), .reset(Reset));
  J_K_Flip_Flop j_k_ff_3 (
    .J(R6), .clk(CLK), .K(j_k_ff_2_qn), .Q(R5), .Qn(j_k_ff_3_qn), .preset(Preset), .en(Enable), .reset(Reset));
  J_K_Flip_Flop j_k_ff_4 (
    .J(R5), .clk(CLK), .K(j_k_ff_3_qn), .Q(R4), .Qn(j_k_ff_4_qn), .preset(Preset), .en(Enable), .reset(Reset));
  J_K_Flip_Flop j_k_ff_5 (
    .J(R4), .clk(CLK), .K(j_k_ff_4_qn), .Q(R3), .Qn(j_k_ff_5_qn), .preset(Preset), .en(Enable), .reset(Reset));
  J_K_Flip_Flop j_k_ff_6 (
    .J(R3), .clk(CLK), .K(j_k_ff_5_qn), .Q(R2), .Qn(j_k_ff_6_qn), .preset(Preset), .en(Enable), .reset(Reset));
  J_K_Flip_Flop j_k_ff_7 (
    .J(R2), .clk(CLK), .K(j_k_ff_6_qn), .Q(R1), .Qn(j_k_ff_7_qn), .preset(Preset), .en(Enable), .reset(Reset));
  J_K_Flip_Flop j_k_ff_8 (
    .J(R1), .clk(CLK), .K(j_k_ff_7_qn), .Q(R0), .preset(Preset), .en(Enable), .reset(Reset));  // open: Qn
endmodule
