// Logisim project 8-bit_5 register multiplaxer.circ as structural Verilog: 1 circuit, main circuit main
module main (
  input  [2:0] in_1,
  input  in_2,
  input  S4,
  input  S3,
  input  S2,
  input  S1,
  input  S0,
  input  Preset,
  input  Enable,
  input  reset,
  output out_11,
  output out_12,
  output out_13,
  output out_14,
  output out_15,
  output out_16,
  output out_17,
  output out_18
);

  wire CLK_out, main_1_r0, main_1_r1, main_1_r2, main_1_r3, main_1_r4, main_1_r5, main_1_r6, main_1_r7,
       main_2_r0, main_2_r1, main_2_r2, main_2_r3, main_2_r4, main_2_r5, main_2_r6, main_2_r7, main_3_r0,
       main_3_r1, main_3_r2, main_3_r3, main_3_r4, main_3_r5, main_3_r6, main_3_r7, main_4_r0, main_4_r1,
       main_4_r2, main_4_r3, main_4_r4, main_4_r5, main_4_r6, main_4_r7, main_5_r0, main_5_r1, main_5_r2,
       main_5_r3, main_5_r4, main_5_r5, main_5_r6, main_5_r7;

  Clock CLK (.out(CLK_out));
  Multiplexer #(.select(3)) multiplexer_1 (
    .in0(main_1_r7), .in1(main_2_r7), .in2(main_3_r7), .in3(main_4_r7), .in4(main_5_r7), .in5(1'b0),
    .in6(1'b0), .in7(1'b0), .out(out_11), .sel(in_1), .en(in_2));
  _8_bit_register_main main_1 (
    .Input(S4), .CLK(CLK_out), .Preset(Preset), .Enable(Enable), .Reset(reset), .R7(main_1_r7),
    .R6(main_1_r6), .R5(main_1_r5), .R4(main_1_r4), .R3(main_1_r3), .R2(main_1_r2), .R1(main_1_r1),
    .R0(main_1_r0));
  Multiplexer #(.select(3)) multiplexer_2 (
    .in0(main_1_r6), .in1(main_2_r6), .in2(main_3_r6), .in3(main_4_r6), .in4(main_5_r6), .in5(1'b0),
    .in6(1'b0), .in7(1'b0), .out(out_12), .sel(in_1), .en(in_2));
  _8_bit_register_main main_2 (
    .Input(S3), .CLK(CLK_out), .Preset(Preset), .Enable(Enable), .Reset(reset), .R7(main_2_r7),
    .R6(main_2_r6), .R5(main_2_r5), .R4(main_2_r4), .R3(main_2_r3), .R2(main_2_r2), .R1(main_2_r1),
    .R0(main_2_r0));
  Multiplexer #(.select(3)) multiplexer_3 (
    .in0(main_1_r5), .in1(main_2_r5), .in2(main_3_r5), .in3(main_4_r5), .in4(main_5_r5), .in5(1'b0),
    .in6(1'b0), .in7(1'b0), .out(out_13), .sel(in_1), .en(in_2));
  Multiplexer #(.select(3)) multiplexer_4 (
    .in0(main_1_r4), .in1(main_2_r4), .in2(main_3_r4), .in3(main_4_r4), .in4(main_5_r4), .in5(1'b0),
    .in6(1'b0), .in7(1'b0), .out(out_14), .sel(in_1), .en(in_2));
  _8_bit_register_main main_3 (
    .Input(S2), .CLK(CLK_out), .Preset(Preset), .Enable(Enable), .Reset(reset), .R7(main_3_r7),
    .R6(main_3_r6), .R5(main_3_r5), .R4(main_3_r4), .R3(main_3_r3), .R2(main_3_r2), .R1(main_3_r1),
    .R0(main_3_r0));
  Multiplexer #(.select(3)) multiplexer_5 (
    .in0(main_1_r3), .in1(main_2_r3), .in2(main_3_r3), .in3(main_4_r3), .in4(main_5_r3), .in5(1'b0),
    .in6(1'b0), .in7(1'b0), .out(out_15), .sel(in_1), .en(in_2));
  _8_bit_register_main main_4 (
    .Input(S1), .CLK(CLK_out), .Preset(Preset), .Enable(Enable), .Reset(reset), .R7(main_4_r7),
    .R6(main_4_r6), .R5(main_4_r5), .R4(main_4_r4), .R3(main_4_r3), .R2(main_4_r2), .R1(main_4_r1),
    .R0(main_4_r0));
  Multiplexer #(.select(3)) multiplexer_6 (
    .in0(main_1_r2), .in1(main_2_r2), .in2(main_3_r2), .in3(main_4_r2), .in4(main_5_r2), .in5(1'b0),
    .in6(1'b0), .in7(1'b0), .out(out_16), .sel(in_1), .en(in_2));
  _8_bit_register_main main_5 (
    .Input(S0), .CLK(CLK_out), .Preset(Preset), .Enable(Enable), .Reset(reset), .R7(main_5_r7),
    .R6(main_5_r6), .R5(main_5_r5), .R4(main_5_r4), .R3(main_5_r3), .R2(main_5_r2), .R1(main_5_r1),
    .R0(main_5_r0));
  Multiplexer #(.select(3)) multiplexer_7 (
    .in0(main_1_r1), .in1(main_2_r1), .in2(main_3_r1), .in3(main_4_r1), .in4(main_5_r1), .in5(1'b0),
    .in6(1'b0), .in7(1'b0), .out(out_17), .sel(in_1), .en(in_2));
  Multiplexer #(.select(3)) multiplexer_8 (
    .in0(main_1_r0), .in1(main_2_r0), .in2(main_3_r0), .in3(main_4_r0), .in4(main_5_r0), .in5(1'b0),
    .in6(1'b0), .in7(1'b0), .out(out_18), .sel(in_1), .en(in_2));
endmodule
