// Logisim project Boolean(A'[B+C]).circ as structural Verilog: 1 circuit, main circuit main
module main (
  input  in_1,
  input  in_2,
  input  in_3,
  output out_4
);

  wire not_1_out, or_1_out;

  not not_1 (not_1_out, in_1);
  or or_1 (or_1_out, in_2, in_3);
  and and_1 (out_4, not_1_out, or_1_out);

  // Notes on the sheet:
  //   Name:- Dwij desai
  //   En. No: 2316212107
  //   2nd Sem(BDA)
  //   Boolean(A'[B+C]])
endmodule
