// Logisim project FS.circ as structural Verilog: 1 circuit, main circuit main
module main (
  input  A,
  input  B,
  input  Bin,
  output D,
  output Bo
);

  wire and_1_out, and_2_out, and_3_out, not_1_out, xor_1_out;

  not not_1 (not_1_out, A);
  xor xor_1 (xor_1_out, A, B);
  and and_1 (and_1_out, not_1_out, B);
  and and_2 (and_2_out, not_1_out, Bin);
  and and_3 (and_3_out, Bin, B);
  xor xor_2 (D, xor_1_out, Bin);
  or or_1 (Bo, and_1_out, and_2_out, and_3_out);

  // Notes on the sheet:
  //   Name:- Dwij desai
  //   En. No: 23162121027
  //   2nd Sem(BDA)
  //   FS
endmodule
