// Logisim project Full adder without using XOR.circ as structural Verilog: 1 circuit, main circuit main
module main (
  input  A,
  input  B,
  input  Cin,
  output S,
  output Co
);

  wire and_1_out, and_2_out, and_3_out;

  and and_1 (and_1_out, A, B);
  and and_2 (and_2_out, A, Cin);
  and and_3 (and_3_out, Cin, B);
  Half_adder_with_out_XOR_main main_1 (.A(A), .B(B), .Cin(Cin), .out_4(S));
  or or_1 (Co, and_1_out, and_2_out, and_3_out);

  // Notes on the sheet:
  //   Name:- Dwij deasi
  //   En. No: 23162121027
  //   2nd sem(BDA)
  //   FA
endmodule
