// Logisim project HA.circ as structural Verilog: 1 circuit, main circuit main
module main (
  input  A,
  input  B,
  output sum,
  output carry
);

  xor xor_1 (sum, A, B);
  and and_1 (carry, A, B);

  // Notes on the sheet:
  //   Name:- Dwij deasi
  //   En. No: 23162121027
  //   2nd sem(BDA)
  //   HA
endmodule
