// Logisim project HS.circ as structural Verilog: 1 circuit, main circuit main
module main (
  input  A,
  input  B,
  output differnce,
  output borrow
);

  wire not_1_out;

  not not_1 (not_1_out, A);
  xor xor_1 (differnce, A, B);
  and and_1 (borrow, not_1_out, B);

  // Notes on the sheet:
  //   Name:- Dwij deasi
  //   En. No: 23162121027
  //   2nd sem(BDA)
  //   HS
endmodule
