// Logisim project Half adder with out XOR.circ as structural Verilog: 1 circuit, main circuit main
module main (
  input  A,
  input  B,
  input  Cin,
  output out_4
);

  wire A_prime_B_prime_C_out, A_prime_BC_prime_out, AB_prime_C_prime_out, ABC_out, not_1_out, not_2_out,
       not_3_out;

  not not_1 (not_1_out, A);
  not not_2 (not_2_out, B);
  not not_3 (not_3_out, Cin);
  and A_prime_B_prime_C (A_prime_B_prime_C_out, not_1_out, not_2_out, Cin);
  and A_prime_BC_prime (A_prime_BC_prime_out, not_1_out, B, not_3_out);
  and AB_prime_C_prime (AB_prime_C_prime_out, A, not_2_out, not_3_out);
  and ABC (ABC_out, A, B, Cin);
  or or_1 (out_4, A_prime_B_prime_C_out, A_prime_BC_prime_out, AB_prime_C_prime_out, ABC_out);

  // Notes on the sheet:
  //   Name:- Dwij desai
  //   En. No: 23162121027
  //   2nd Sem(BDA)
  //   Half adder without XOR
endmodule
