// Logisim project Nand as Xor.circ as structural Verilog: 1 circuit, main circuit main
module main (
  input  A,
  input  B,
  output Out_X_OR
);

  wire nand_1_out, nand_2_out, nand_3_out;

  nand nand_1 (nand_1_out, A, B);
  nand nand_2 (nand_2_out, A, nand_1_out);
  nand nand_3 (nand_3_out, nand_1_out, B);
  nand nand_4 (Out_X_OR, nand_2_out, nand_3_out);

  // Notes on the sheet:
  //   Name:- Dwij Desai
  //   En. No: 23162121027
  //   2nd Sem(BDA)
  //   Nand as Xor
endmodule
