// Logisim project Short Boolean(A'[B+C]).circ as structural Verilog: 1 circuit, main circuit main
module main (
  input  A,
  input  B,
  input  C,
  output Out
);

  Boolean_A__B_C___main main_1 (.in_1(A), .in_2(B), .in_3(C), .out_4(Out));

  // Notes on the sheet:
  //   Name: Dwij deasi
  //   En. No: 23162121027
  //   2nd Sem(BDA)
endmodule
