// Logisim project short Aand as Xor.circ as structural Verilog: 1 circuit, main circuit main
module main (
  input  A,
  input  B,
  output Out_XOR
);

  Nand_as_Xor_main main_1 (.A(A), .B(B), .Out_X_OR(Out_XOR));

  // Notes on the sheet:
  //   Name:- Dwij desai
  //   En. No: 23162121027
  //   2nd Sem(BDA)
  //   23162121027
  //   Dwij deasi
  //   2nd sem
endmodule
