// Logisim project short FA.circ as structural Verilog: 1 circuit, main circuit main
module main (
  input  B,
  input  A,
  input  Cin,
  output Cout,
  output S
);

  FA_main main_1 (.S(S));  // open: A, B, Cin, Co

  // Notes on the sheet:
  //   Name:- Dwij deasi
  //   En. No: 23162121027
  //   2nd Sem(BDA)
endmodule
