// Logisim project short FS.circ as structural Verilog: 1 circuit, main circuit main
module main (
  input  B,
  input  A,
  input  Bin,
  output Bo,
  output D
);

  FS_main main_1 (.A(A), .B(B), .Bin(Bin), .D(D), .Bo(Bo));

  // Notes on the sheet:
  //   Name:- Dwij desai
  //   En. No: 23162121027
  //   2nd Sem(BDA)
endmodule
