// Logisim project short HA.circ as structural Verilog: 1 circuit, main circuit main
module main (
  input  B,
  input  A,
  output carry,
  output sum
);

  HA_main main_1 (.A(A), .B(B), .sum(sum), .carry(carry));

  // Notes on the sheet:
  //   2nd sem(BDA)
  //   Name:- Dwij desai
  //   En. No: 23162121027
endmodule
