// Logisim project short HS.circ as structural Verilog: 1 circuit, main circuit main
module main (
  input  B,
  input  A,
  output Borrow,
  output Differnce
);

  HS_main main_1 (.A(A), .B(B), .differnce(Differnce), .borrow(Borrow));
endmodule
