// Logisim project Decrementer.circ as structural Verilog: 1 circuit, main circuit main
module main (
  input  A2,
  input  A1,
  input  A0,
  input  A3,
  output S4,
  output S3,
  output S2,
  output S1,
  output S0
);

  wire main_2_co, main_3_co, main_4_co;

  FA_main main_1 (.A(A3), .B(1'b1), .Cin(main_2_co), .S(S3), .Co(S4));
  FA_main main_2 (.A(A2), .B(1'b1), .Cin(main_3_co), .S(S2), .Co(main_2_co));
  FA_main main_3 (.A(A1), .B(1'b1), .Cin(main_4_co), .S(S1), .Co(main_3_co));
  FA_main main_4 (.A(A0), .B(1'b1), .Cin(1'b0), .S(S0), .Co(main_4_co));

  // Notes on the sheet:
  //   Name:- Dwij desai  En.No:23162121027 (BDA)
  //   Decrement
endmodule
