// Logisim project FA.circ as structural Verilog: 1 circuit, main circuit main
module main (
  input  A,
  input  B,
  input  Cin,
  output S,
  output Co
);

  wire and_1_out, and_2_out, and_3_out, xor_1_out;

  xor xor_1 (xor_1_out, A, B);
  and and_1 (and_1_out, A, B);
  and and_2 (and_2_out, A, Cin);
  and and_3 (and_3_out, Cin, B);
  xor xor_2 (S, xor_1_out, Cin);
  or or_1 (Co, and_1_out, and_2_out, and_3_out);

  // Notes on the sheet:
  //   Name:- Dwij deasi
  //   En. No: 23162121027
  //   2nd sem(BDA)
  //   Full Adder type-1
endmodule
