// Logisim project Fulladder for Ripple carry adder.circ as structural Verilog: 1 circuit, main circuit main
module main (
  input  A3,
  input  B3,
  input  A2,
  input  B2,
  input  A1,
  input  B1,
  input  A0,
  input  B0,
  input  Cin,
  output Cout3,
  output S3,
  output S2,
  output S1,
  output S0
);

  wire and_1_out, and_2_out, and_3_out, and_4_out, and_5_out, and_6_out, and_7_out, and_8_out, Cout0_out,
       Cout1_out, Cout2_out, xor_2_out, xor_4_out, xor_6_out, xor_8_out;

  xor xor_1 (S3, xor_2_out, Cout2_out);
  or u_Cout3 (Cout3, and_1_out, and_2_out);
  xor xor_2 (xor_2_out, A3, B3);
  and and_1 (and_1_out, Cout2_out, xor_2_out);
  and and_2 (and_2_out, B3, A3);
  xor xor_3 (S2, xor_4_out, Cout1_out);
  or Cout2 (Cout2_out, and_3_out, and_4_out);
  xor xor_4 (xor_4_out, A2, B2);
  and and_3 (and_3_out, Cout1_out, xor_4_out);
  and and_4 (and_4_out, B2, A2);
  xor xor_5 (S1, xor_6_out, Cout0_out);
  or Cout1 (Cout1_out, and_5_out, and_6_out);
  xor xor_6 (xor_6_out, A1, B1);
  and and_5 (and_5_out, Cout0_out, xor_6_out);
  and and_6 (and_6_out, B1, A1);
  xor xor_7 (S0, xor_8_out, Cin);
  or Cout0 (Cout0_out, and_7_out, and_8_out);
  xor xor_8 (xor_8_out, A0, B0);
  and and_7 (and_7_out, Cin, xor_8_out);
  and and_8 (and_8_out, B0, A0);

  // Notes on the sheet:
  //   Name:- Dwij desai
  //   En. No: 23162121027
  //   2nd sem (BDA)
  //   Fulladder for Ripple carry adder
endmodule
