// Logisim project Short Ripple carry adder.circ as structural Verilog: 1 circuit, main circuit main
module main (
  input  B3,
  input  A3,
  input  B2,
  input  A2,
  input  B1,
  input  A1,
  input  B0,
  input  A0,
  input  Cin,
  output S4,
  output S3,
  output S2,
  output S1,
  output S0
);

  wire main_2_p2, main_3_p2, main_4_p2;

  // FA_main main_1: pin names not known; wires that end beside it: S4, S3
  // FA_main main_2: pin names not known; wires that end beside it: S4, main_2_p2, main_2_p2, S2
  // FA_main main_3: pin names not known; wires that end beside it: main_2_p2, main_3_p2, main_3_p2, S1
  // FA_main main_4: pin names not known; wires that end beside it: main_3_p2, main_4_p2, main_4_p2, S0

  // Notes on the sheet:
  //   2nd sem (BDA)
  //   Name:- Dwij desai
  //   Ripple carry adder using sub cricuit
  //   En. No: 23162121027
endmodule
