// Logisim project Half-subtacter.circ as structural Verilog: 1 circuit, main circuit main
module main (
  input  A,
  input  B,
  output Differcene,
  output carry
);

  wire not_1_out;

  not not_1 (not_1_out, B);
  xor xor_1 (Differcene, A, B);
  and and_1 (carry, A, not_1_out);

  // Notes on the sheet:
  //   Half-Subtracter
  //   Name:- Dwij deasi  En. No:- 23162121027  2nd sem (BDA)
endmodule
