// Logisim project Parallel Binary Full-subtracter(using full-adder).circ as structural Verilog: 1 circuit, main circuit main
module main (
  input  A3,
  input  A2,
  input  A1,
  input  A0,
  input  B3,
  input  B2,
  input  B1,
  input  B0,
  output carry,
  output D3,
  output D2,
  output D1,
  output out_13
);

  wire main_2_p1, main_3_p1, main_4_p1, not_1_out, not_2_out, not_3_out, not_4_out;

  not not_1 (not_1_out, B3);
  // FA_main main_1: pin names not known; wires that end beside it: carry, D3
  not not_2 (not_2_out, B2);
  // FA_main main_2: pin names not known; wires that end beside it: main_2_p1, main_2_p1, D2
  not not_3 (not_3_out, B1);
  // FA_main main_3: pin names not known; wires that end beside it: main_3_p1, main_3_p1, D1
  not not_4 (not_4_out, B0);
  // FA_main main_4: pin names not known; wires that end beside it: main_4_p1, main_4_p1, out_13

  // Notes on the sheet:
  //   Parallel Binary Full-subtracter(using full-adder)
  //   Name:- Dwij deasi  En. No:- 23162121027  2nd sem (BDA)
endmodule
