// Logisim project Parallel Binary Full-subtracter(using mod control).circ as structural Verilog: 1 circuit, main circuit main
module main (
  input  in_1,
  input  A3,
  input  A2,
  input  A1,
  input  A0,
  input  B3,
  input  B2,
  input  B1,
  input  B0,
  output carry,
  output D3,
  output D2,
  output D1,
  output out_14
);

  wire main_2_p1, main_3_p1, main_4_p1, xor_1_out, xor_2_out, xor_3_out, xor_4_out;

  xor xor_1 (xor_1_out, B3, in_1);
  // FA_main main_1: pin names not known; wires that end beside it: carry, D3
  xor xor_2 (xor_2_out, B2, in_1);
  // FA_main main_2: pin names not known; wires that end beside it: main_2_p1, main_2_p1, D2
  xor xor_3 (xor_3_out, B1, in_1);
  // FA_main main_3: pin names not known; wires that end beside it: main_3_p1, main_3_p1, D1
  xor xor_4 (xor_4_out, B0, in_1);
  // FA_main main_4: pin names not known; wires that end beside it: main_4_p1, main_4_p1, out_14

  // Notes on the sheet:
  //   Name:- Dwij deasi  En. No:- 23162121027  2nd sem (BDA)
  //   Parallel Binary Full-subtracter(using mod control)
endmodule
