// Logisim project Parallel Binary Subtractors(Ripple Carry).circ as structural Verilog: 1 circuit, main circuit main
module main (
  input  B3,
  input  A3,
  input  B2,
  input  A2,
  input  B1,
  input  A1,
  input  B0,
  input  A0,
  output Bout,
  output D3,
  output D2,
  output D1,
  output D0
);

  wire main_2_carry, main_3_carry, main_4_carry;

  full_subtracter_using_half_subtracter__main main_1 (
    .A(A3), .B(B3), .Bin(main_2_carry), .Differcene(D3), .carry(Bout));
  full_subtracter_using_half_subtracter__main main_2 (
    .A(A2), .B(B2), .Bin(main_3_carry), .Differcene(D2), .carry(main_2_carry));
  full_subtracter_using_half_subtracter__main main_3 (
    .A(A1), .B(B1), .Bin(main_4_carry), .Differcene(D1), .carry(main_3_carry));
  Half_subtacter_main main_4 (.A(A0), .B(B0), .Differcene(D0), .carry(main_4_carry));

  // Notes on the sheet:
  //   Name:- Dwij deasi
  //   En. No:- 23162121027
  //   2nd sem (BDA)
  //   Parallel Binary Subtractors(Ripple Carry)
endmodule
