// Logisim project full-subtracter(using half-subtracter).circ as structural Verilog: 1 circuit, main circuit main
module main (
  input  A,
  input  B,
  input  Bin,
  output Differcene,
  output carry
);

  wire and_1_out, and_2_out, not_1_out, not_2_out, xor_1_out;

  not not_1 (not_1_out, A);
  xor xor_1 (xor_1_out, A, B);
  and and_1 (and_1_out, not_1_out, B);
  not not_2 (not_2_out, xor_1_out);
  xor xor_2 (Differcene, xor_1_out, Bin);
  and and_2 (and_2_out, Bin, not_2_out);
  or or_1 (carry, and_2_out, and_1_out);

  // Notes on the sheet:
  //   full-subtracter(using half-subtracter)
  //   Name:- Dwij deasi  En. No:- 23162121027  2nd sem (BDA)
endmodule
