// Logisim project Practical_4(full adder).circ as structural Verilog: 1 circuit, main circuit main
module main (
  input  A,
  input  B,
  input  Ci,
  output Si,
  output Ci_1
);

  wire and_1_out, Gi_out, Pi_out;

  xor Pi (Pi_out, A, B);
  and Gi (Gi_out, A, B);
  xor xor_1 (Si, Pi_out, Ci);
  and and_1 (and_1_out, Pi_out, Ci);
  or or_1 (Ci_1, and_1_out, Gi_out);
endmodule
