// Logisim project Q-1.circ as structural Verilog: 1 circuit, main circuit main
module main (
  input  C0,
  input  A0,
  input  B0,
  input  A1,
  input  B1,
  input  A2,
  input  B2,
  input  A3,
  input  B3,
  output S1,
  output S2,
  output S3,
  output S4,
  output C4
);

  wire and_1_out, and_2_out, and_3_out, and_4_out, main_1_c1, main_1_c2, main_1_c3, xor_1_out, xor_2_out,
       xor_3_out, xor_4_out;

  xor xor_1 (xor_1_out, A0, B0);
  and and_1 (and_1_out, A0, B0);
  xor xor_2 (xor_2_out, A1, B1);
  and and_2 (and_2_out, A1, B1);
  xor xor_3 (xor_3_out, A2, B2);
  and and_3 (and_3_out, A2, B2);
  xor xor_4 (xor_4_out, A3, B3);
  and and_4 (and_4_out, A3, B3);
  Practical_4_Q_1__4_bit_adder__main main_1 (
    .P3(xor_4_out), .Gi_3(and_4_out), .P2(xor_3_out), .G2(and_3_out), .P1(xor_2_out), .G1(and_2_out),
    .P0(xor_1_out), .G0(and_1_out), .C0(C0), .C4(C4), .C3(main_1_c3), .C2(main_1_c2), .C1(main_1_c1));
  xor xor_5 (S1, C0, xor_1_out);
  xor xor_6 (S2, main_1_c1, xor_2_out);
  xor xor_7 (S3, main_1_c3, xor_3_out);
  xor xor_8 (S4, main_1_c2, xor_4_out);

  // Notes on the sheet:
  //   Dwij desai 23162121027 2nd sem(BDA) 
endmodule
