// Logisim project Case-1.circ as structural Verilog: 1 circuit, main circuit main
module main (
  input  F,
  input  E,
  input  D,
  input  C,
  input  B,
  input  A,
  input  G,
  output cout,
  output S1,
  output S0
);

  wire FA1_co, FA1_s, FA2_co, FA2_s, FA4_co;

  Full_Adder_vertical_main FA1 (.Cin(D), .B(E), .A(F), .Co(FA1_co), .S(FA1_s));
  Full_Adder_vertical_main FA3 (.Cin(FA4_co), .B(FA2_co), .A(FA1_co), .Co(cout), .S(S1));
  Full_Adder_vertical_main FA2 (.Cin(A), .B(B), .A(C), .Co(FA2_co), .S(FA2_s));
  Full_Adder_vertical_main FA4 (.Cin(G), .B(FA2_s), .A(FA1_s), .Co(FA4_co), .S(S0));

  // Notes on the sheet:
  //   Dwij deasi 27   2nd-sem (BDA)
endmodule
