// Logisim project Case-3.circ as structural Verilog: 1 circuit, main circuit main
module main (
  input  A3,
  input  A2,
  input  A1,
  input  A0,
  input  B3,
  input  B2,
  input  B1,
  input  B0,
  input  E3,
  input  E2,
  input  E1,
  input  E0,
  input  C3,
  input  C2,
  input  C1,
  input  C0,
  input  D3,
  input  D2,
  input  D1,
  input  D0,
  output S6,
  output S5,
  output S4,
  output S3,
  output S2,
  output S1,
  output S0
);

  wire FA1_co, FA1_s, FA2_co, FA2_s, FA3_co, FA3_s, FA4_co, FA4_s, FA5_co, FA5_s, FA6_co, FA6_s, FA7_co,
       FA7_s, FA8_co, FA8_s, FA9_co, main_2_s0, main_2_s1, main_2_s2, main_2_s3, main_2_s4;

  Full_Adder_vertical_main FA1 (.Cin(A3), .B(B3), .A(C3), .Co(FA1_co), .S(FA1_s));
  Full_Adder_vertical_main FA2 (.Cin(A2), .B(B2), .A(C2), .Co(FA2_co), .S(FA2_s));
  Full_Adder_vertical_main FA3 (.Cin(A1), .B(B1), .A(C1), .Co(FA3_co), .S(FA3_s));
  Full_Adder_vertical_main FA4 (.Cin(A0), .B(B0), .A(C0), .Co(FA4_co), .S(FA4_s));
  Full_Adder_vertical_main FA5 (.Cin(main_2_s4), .B(1'b0), .A(FA1_co), .Co(FA5_co), .S(FA5_s));
  Full_Adder_vertical_main FA6 (.Cin(main_2_s3), .B(FA1_s), .A(FA2_co), .Co(FA6_co), .S(FA6_s));
  Short_Ripple_carry_adder_5_bit__main main_1 (
    .B3(FA5_s), .A3(FA6_co), .B2(FA6_s), .A2(FA7_co), .B1(FA7_s), .A1(FA8_co), .B0(FA8_s), .A0(FA9_co),
    .S4(S5), .S3(S4), .S2(S3), .S1(S2), .S0(S1), .Cin(1'b0), .B4(1'b0), .A4(FA5_co), .S5(S6));
  Full_Adder_vertical_main FA7 (.Cin(main_2_s2), .B(FA2_s), .A(FA3_co), .Co(FA7_co), .S(FA7_s));
  Full_Adder_vertical_main FA8 (.Cin(main_2_s1), .B(FA3_s), .A(FA4_co), .Co(FA8_co), .S(FA8_s));
  Full_Adder_vertical_main FA9 (.Cin(main_2_s0), .B(FA4_s), .A(1'b0), .Co(FA9_co), .S(S0));
  Short_Ripple_carry_adder_main main_2 (
    .B3(E3), .A3(D3), .B2(E2), .A2(D2), .B1(E1), .A1(D1), .B0(E0), .A0(D0), .S4(main_2_s4), .S3(main_2_s3),
    .S2(main_2_s2), .S1(main_2_s1), .S0(main_2_s0), .Cin(1'b0));

  // Notes on the sheet:
  //   Dwij desai 27  2nd-sem(BDA)
  //   A= 1010 = 10
  //   B= 0011 = 3
  //   C= 0110 = 6
  //   D= 1000 = 8
  //   E= 1111 = 15
  //   sum= 0101010 = 42
endmodule
