// Logisim project Full Adder vertical.circ as structural Verilog: 1 circuit, main circuit main
module main (
  input  Cin,
  input  B,
  input  A,
  output S,
  output Co
);

  wire and_1_out, and_2_out, xor_2_out;

  and and_1 (and_1_out, A, B);
  and and_2 (and_2_out, Cin, xor_2_out);
  or or_1 (Co, and_1_out, and_2_out);
  xor xor_1 (S, Cin, xor_2_out);
  xor xor_2 (xor_2_out, B, A);

  // Notes on the sheet:
  //   Name:- Dwij deasi
  //   En. No: 23162121027
  //   2nd sem(BDA)
  //   Full Adder vertical
endmodule
