// Logisim project Short Ripple carry adder(5-bit).circ as structural Verilog: 1 circuit, main circuit main
// 5-bit
module main (
  input  B4,
  input  A4,
  input  B3,
  input  A3,
  input  B2,
  input  A2,
  input  B1,
  input  A1,
  input  B0,
  input  A0,
  input  Cin,
  output S5,
  output S4,
  output S3,
  output S2,
  output S1,
  output S0
);

  wire main_2_p1, main_3_p1, main_4_p1, main_5_p1;

  // FA_main main_1: pin names not known; wires that end beside it: S5, S4
  // FA_main main_2: pin names not known; wires that end beside it: main_2_p1, main_2_p1, S3
  // FA_main main_3: pin names not known; wires that end beside it: main_3_p1, S2
  // FA_main main_4: pin names not known; wires that end beside it: main_4_p1, S1
  // FA_main main_5: pin names not known; wires that end beside it: main_5_p1, S0

  // Notes on the sheet:
  //   2nd sem (BDA)
  //   Name:- Dwij desai
  //   Ripple carry adder using sub cricuit
  //   En. No: 23162121027
endmodule
