// Logisim project addtion of three 4-bit number (case-2).circ as structural Verilog: 1 circuit, main circuit main
module main (
  input  c3,
  input  b3,
  input  a3,
  input  c2,
  input  b2,
  input  a2,
  input  c1,
  input  b1,
  input  a1,
  input  c0,
  input  b0,
  input  a0,
  input  cin,
  output cout,
  output S5,
  output S4,
  output S3,
  output S2,
  output S1,
  output S0
);

  wire FA0_co, FA1_co, FA1_s, FA2_co, FA2_s, FA3_co, FA3_s;

  Full_Adder_vertical_main FA3 (.Cin(a3), .B(b3), .A(c3), .Co(FA3_co), .S(FA3_s));
  Full_Adder_vertical_main FA2 (.Cin(a2), .B(b2), .A(c2), .Co(FA2_co), .S(FA2_s));
  Short_Ripple_carry_adder_main main_1 (
    .B3(1'b0), .A3(FA3_co), .B2(FA3_s), .A2(FA2_co), .B1(FA2_s), .A1(FA1_co), .B0(FA1_s), .A0(FA0_co),
    .S4(cout), .S3(S4), .S2(S3), .S1(S2), .S0(S1), .Cin(cin));
  Full_Adder_vertical_main FA1 (.Cin(a1), .B(b1), .A(c1), .Co(FA1_co), .S(FA1_s));
  Full_Adder_vertical_main FA0 (.Cin(a0), .B(b0), .A(c0), .Co(FA0_co), .S(S0));

  assign S5 = cout;

  // Notes on the sheet:
  //   Dwij desai 27  2nd-sem(BDA)
endmodule
