// Logisim project Case-1.circ as structural Verilog: 1 circuit, main circuit main
module main (
  input  A1,
  input  A0,
  input  B1,
  input  B0,
  output S3,
  output S2,
  output S1,
  output S0
);

  wire AND1_out, AND2_out, AND3_out, main_2_carry;

  short_HA_main main_1 (.carry(S3), .B(AND3_out), .A(main_2_carry), .sum(S2));
  and AND3 (AND3_out, A1, A0);
  and AND1 (AND1_out, A1, B0);
  and AND2 (AND2_out, B1, A0);
  short_HA_main main_2 (.carry(main_2_carry), .B(AND2_out), .A(AND1_out), .sum(S1));
  and AND0 (S0, B1, B0);

  // Notes on the sheet:
  //   3 * 2 = 6
  //   Dwij desai 27 2nd-sem(BDA)
endmodule
