// Logisim project Case-2.circ as structural Verilog: 1 circuit, main circuit main
module main (
  input  A3,
  input  A2,
  input  A1,
  input  A0,
  input  B3,
  input  B2,
  input  B1,
  input  B0,
  output S7,
  output S6,
  output S5,
  output S4,
  output S3,
  output S2,
  output S1,
  output S0
);

  wire AND_2_out, AND_3_out, AND_4_out, AND_5_out, AND_6_out, AND_7_out, AND_8_out, AND_9_out, AND_10_out,
       AND_11_out, AND_12_out, AND_13_out, AND_14_out, AND_15_out, AND_out, main_2_co, main_2_s, main_3_s,
       main_4_co, main_4_s, main_5_co, main_5_s, main_6_carry, main_7_carry, main_7_sum, main_8_co, main_8_s,
       main_9_s, main_10_s, main_11_carry, main_11_sum, main_12_carry;

  and AND (AND_out, A3, B3);
  FA_main main_1 (.A(main_2_s), .B(AND_out), .Cin(main_3_s), .S(S7), .Co(S6));
  and AND_2 (AND_2_out, B3, B2);
  and AND_3 (AND_3_out, A2, B2);
  FA_main main_2 (.A(AND_3_out), .B(AND_2_out), .Cin(main_4_s), .S(main_2_s), .Co(main_2_co));
  FA_main main_3 (.A(main_5_s), .B(main_2_co), .Cin(main_6_carry), .S(main_3_s), .Co(S5));
  and AND_4 (AND_4_out, B3, B1);
  and AND_5 (AND_5_out, A2, B2);
  FA_main main_4 (.A(AND_6_out), .B(AND_5_out), .Cin(main_7_carry), .S(main_4_s), .Co(main_4_co));
  FA_main main_5 (.A(main_4_co), .B(AND_4_out), .Cin(main_8_s), .S(main_5_s), .Co(main_5_co));
  short_HA_main main_6 (.carry(main_6_carry), .B(main_5_co), .A(main_9_s), .sum(S4));
  and AND_6 (AND_6_out, A1, B2);
  and AND_7 (AND_7_out, B3, B0);
  and AND_8 (AND_8_out, A0, B3);
  and AND_9 (AND_9_out, A1, B2);
  and AND_10 (AND_10_out, A2, B1);
  short_HA_main main_7 (.carry(main_7_carry), .B(AND_9_out), .A(AND_8_out), .sum(main_7_sum));
  FA_main main_8 (.A(main_7_sum), .B(AND_10_out), .Cin(main_11_carry), .S(main_8_s), .Co(main_8_co));
  FA_main main_9 (.A(main_8_co), .B(AND_7_out), .Cin(main_10_s), .S(main_9_s), .Co(S3));
  and AND_11 (AND_11_out, A2, B0);
  FA_main main_10 (.A(main_11_sum), .B(AND_11_out), .Cin(main_12_carry), .S(main_10_s), .Co(S2));
  and AND_12 (AND_12_out, A0, B2);
  and AND_13 (AND_13_out, A1, B1);
  short_HA_main main_11 (.carry(main_11_carry), .B(AND_13_out), .A(AND_12_out), .sum(main_11_sum));
  and AND_14 (AND_14_out, A1, B0);
  and AND_15 (AND_15_out, A0, B1);
  short_HA_main main_12 (.carry(main_12_carry), .B(AND_15_out), .A(AND_14_out), .sum(S1));
  and AND_16 (S0, A0, B0);

  // Notes on the sheet:
  //   Dwij desai 27 2nd-sem(BDA)
  //   9 = 1001
  //   x9 = 1001
  //   ----------------
  //   81 = 01010001
endmodule
