// Logisim project case-1.circ as structural Verilog: 1 circuit, main circuit main
module main (
  input  [1:0] in_1,
  input  in_2,
  input  in_3,
  input  in_4,
  input  in_5,
  input  in_6,
  input  in_7,
  input  in_8,
  input  in_9,
  output out_10,
  output out_11,
  output out_12,
  output out_13
);

  wire clock_1_out, main_1_r0, main_1_r1, main_1_r2, main_1_r3, main_2_r0, main_2_r1, main_2_r2, main_2_r3,
       main_3_r0, main_3_r1, main_3_r2, main_3_r3, main_4_r0, main_4_r1, main_4_r2, main_4_r3;

  Clock clock_1 (.out(clock_1_out));
  Multiplexer #(.select(2)) multiplexer_1 (
    .in0(main_1_r3), .in1(main_2_r3), .in2(main_3_r3), .in3(main_4_r3), .out(out_10), .sel(in_1), .en(in_2));
  register_with_chip__main main_1 (
    .in_1(in_3), .CLK(clock_1_out), .PERSET(in_7), .ENABLE(in_8), .RESET(in_9), .R3(main_1_r3),
    .R2(main_1_r2), .R1(main_1_r1), .R0(main_1_r0));
  Multiplexer #(.select(2)) multiplexer_2 (
    .in0(main_1_r2), .in1(main_2_r2), .in2(main_3_r2), .in3(main_4_r2), .out(out_11), .sel(in_1), .en(in_2));
  register_with_chip__main main_2 (
    .in_1(in_4), .CLK(clock_1_out), .PERSET(in_7), .ENABLE(in_8), .RESET(in_9), .R3(main_2_r3),
    .R2(main_2_r2), .R1(main_2_r1), .R0(main_2_r0));
  Multiplexer #(.select(2)) multiplexer_3 (
    .in0(main_1_r1), .in1(main_2_r1), .in2(main_3_r1), .in3(main_4_r1), .out(out_12), .sel(in_1), .en(in_2));
  register_with_chip__main main_3 (
    .in_1(in_5), .CLK(clock_1_out), .PERSET(in_7), .ENABLE(in_8), .RESET(in_9), .R3(main_3_r3),
    .R2(main_3_r2), .R1(main_3_r1), .R0(main_3_r0));
  Multiplexer #(.select(2)) multiplexer_4 (
    .in0(main_1_r0), .in1(main_2_r0), .in2(main_3_r0), .in3(main_4_r0), .out(out_13), .sel(in_1), .en(in_2));
  register_with_chip__main main_4 (
    .in_1(in_6), .CLK(clock_1_out), .PERSET(in_7), .ENABLE(in_8), .RESET(in_9), .R3(main_4_r3),
    .R2(main_4_r2), .R1(main_4_r1), .R0(main_4_r0));

  // Notes on the sheet:
  //   R0 = 1100
  //   R1 = 1001
  //   R2 = 1000
  //   R3 = 0011
endmodule
