// Logisim project case-2.circ as structural Verilog: 1 circuit, main circuit main
module main (
  input  in_1,
  input  [2:0] in_2,
  input  in_3,
  input  in_4,
  input  in_5,
  input  in_6,
  input  in_7,
  input  in_8,
  input  in_9,
  input  in_10,
  input  insert,
  input  Enable,
  input  preset,
  output out_14,
  output out_15,
  output out_16,
  output out_17,
  output out_18,
  output out_19,
  output out_20,
  output out_21
);

  wire clock_1_out, main_1_r0, main_1_r1, main_1_r2, main_1_r3, main_1_r4, main_1_r5, main_1_r6, main_1_r7,
       main_2_r0, main_2_r1, main_2_r2, main_2_r3, main_2_r4, main_2_r5, main_2_r6, main_2_r7, main_3_r0,
       main_3_r1, main_3_r2, main_3_r3, main_3_r4, main_3_r5, main_3_r6, main_3_r7, main_4_r0, main_4_r1,
       main_4_r2, main_4_r3, main_4_r4, main_4_r5, main_4_r6, main_4_r7, main_5_r0, main_5_r1, main_5_r2,
       main_5_r3, main_5_r4, main_5_r5, main_5_r6, main_5_r7, main_6_r0, main_6_r1, main_6_r2, main_6_r3,
       main_6_r4, main_6_r5, main_6_r6, main_6_r7, main_7_r0, main_7_r1, main_7_r2, main_7_r3, main_7_r4,
       main_7_r5, main_7_r6, main_7_r7, main_8_r0, main_8_r1, main_8_r2, main_8_r3, main_8_r4, main_8_r5,
       main_8_r6, main_8_r7;

  Clock clock_1 (.out(clock_1_out));
  Multiplexer #(.select(3)) multiplexer_1 (
    .in0(main_1_r0), .in1(main_2_r0), .in2(main_3_r0), .in3(main_4_r0), .in4(main_5_r0), .in5(main_6_r0),
    .in6(main_7_r0), .in7(main_8_r0), .out(out_14), .sel(in_2), .en(in_1));
  register_8_bit__with_chip__main main_1 (
    .in_1(in_3), .CLK(clock_1_out), .PERSET(insert), .ENABLE(Enable), .RESET(preset), .R7(main_1_r7),
    .R6(main_1_r6), .R5(main_1_r5), .R4(main_1_r4), .R3(main_1_r3), .R2(main_1_r2), .R1(main_1_r1),
    .R0(main_1_r0));
  Multiplexer #(.select(3)) multiplexer_2 (
    .in0(main_1_r1), .in1(main_2_r1), .in2(main_3_r1), .in3(main_4_r1), .in4(main_5_r1), .in5(main_6_r1),
    .in6(main_7_r1), .in7(main_8_r1), .out(out_15), .sel(in_2), .en(in_1));
  register_8_bit__with_chip__main main_2 (
    .in_1(in_4), .CLK(clock_1_out), .PERSET(insert), .ENABLE(Enable), .RESET(preset), .R7(main_2_r7),
    .R6(main_2_r6), .R5(main_2_r5), .R4(main_2_r4), .R3(main_2_r3), .R2(main_2_r2), .R1(main_2_r1),
    .R0(main_2_r0));
  Multiplexer #(.select(3)) multiplexer_3 (
    .in0(main_1_r2), .in1(main_2_r2), .in2(main_3_r2), .in3(main_4_r2), .in4(main_5_r2), .in5(main_6_r2),
    .in6(main_7_r2), .in7(main_8_r2), .out(out_16), .sel(in_2), .en(in_1));
  register_8_bit__with_chip__main main_3 (
    .in_1(in_5), .CLK(clock_1_out), .PERSET(insert), .ENABLE(Enable), .RESET(preset), .R7(main_3_r7),
    .R6(main_3_r6), .R5(main_3_r5), .R4(main_3_r4), .R3(main_3_r3), .R2(main_3_r2), .R1(main_3_r1),
    .R0(main_3_r0));
  Multiplexer #(.select(3)) multiplexer_4 (
    .in0(main_1_r3), .in1(main_2_r3), .in2(main_3_r3), .in3(main_4_r3), .in4(main_5_r3), .in5(main_6_r3),
    .in6(main_7_r3), .in7(main_8_r3), .out(out_17), .sel(in_2), .en(in_1));
  register_8_bit__with_chip__main main_4 (
    .in_1(in_6), .CLK(clock_1_out), .PERSET(insert), .ENABLE(Enable), .RESET(preset), .R7(main_4_r7),
    .R6(main_4_r6), .R5(main_4_r5), .R4(main_4_r4), .R3(main_4_r3), .R2(main_4_r2), .R1(main_4_r1),
    .R0(main_4_r0));
  Multiplexer #(.select(3)) multiplexer_5 (
    .in0(main_1_r4), .in1(main_2_r4), .in2(main_3_r4), .in3(main_4_r4), .in4(main_5_r4), .in5(main_6_r4),
    .in6(main_7_r4), .in7(main_8_r4), .out(out_18), .sel(in_2), .en(in_1));
  register_8_bit__with_chip__main main_5 (
    .in_1(in_7), .CLK(clock_1_out), .PERSET(insert), .ENABLE(Enable), .RESET(preset), .R7(main_5_r7),
    .R6(main_5_r6), .R5(main_5_r5), .R4(main_5_r4), .R3(main_5_r3), .R2(main_5_r2), .R1(main_5_r1),
    .R0(main_5_r0));
  Multiplexer #(.select(3)) multiplexer_6 (
    .in0(main_1_r5), .in1(main_2_r5), .in2(main_3_r5), .in3(main_4_r5), .in4(main_5_r5), .in5(main_6_r5),
    .in6(main_7_r5), .in7(main_8_r5), .out(out_19), .sel(in_2), .en(in_1));
  register_8_bit__with_chip__main main_6 (
    .in_1(in_8), .CLK(clock_1_out), .PERSET(insert), .ENABLE(Enable), .RESET(preset), .R7(main_6_r7),
    .R6(main_6_r6), .R5(main_6_r5), .R4(main_6_r4), .R3(main_6_r3), .R2(main_6_r2), .R1(main_6_r1),
    .R0(main_6_r0));
  register_8_bit__with_chip__main main_7 (
    .in_1(in_9), .CLK(clock_1_out), .PERSET(insert), .ENABLE(Enable), .RESET(preset), .R7(main_7_r7),
    .R6(main_7_r6), .R5(main_7_r5), .R4(main_7_r4), .R3(main_7_r3), .R2(main_7_r2), .R1(main_7_r1),
    .R0(main_7_r0));
  Multiplexer #(.select(3)) multiplexer_7 (
    .in0(main_1_r6), .in1(main_2_r6), .in2(main_3_r6), .in3(main_4_r6), .in4(main_5_r6), .in5(main_6_r6),
    .in6(main_7_r6), .in7(main_8_r6), .out(out_20), .sel(in_2), .en(in_1));
  register_8_bit__with_chip__main main_8 (
    .in_1(in_10), .CLK(clock_1_out), .PERSET(insert), .ENABLE(Enable), .RESET(preset), .R7(main_8_r7),
    .R6(main_8_r6), .R5(main_8_r5), .R4(main_8_r4), .R3(main_8_r3), .R2(main_8_r2), .R1(main_8_r1),
    .R0(main_8_r0));
  Multiplexer #(.select(3)) multiplexer_8 (
    .in0(main_1_r7), .in1(main_2_r7), .in2(main_3_r7), .in3(main_4_r7), .in4(main_5_r7), .in5(main_6_r7),
    .in6(main_7_r7), .in7(main_8_r7), .out(out_21), .sel(in_2), .en(in_1));

  // Notes on the sheet:
  //   000->11111111
  //   001->01111111
  //   010->11111110
  //   011->01111110
  //   100->01111011
  //   101->11110010
  //   110->0110010
  //   111->11000010
endmodule
