// Logisim project register(with chip).circ as structural Verilog: 1 circuit, main circuit main
module main (
  input  in_1,
  input  CLK,
  input  PERSET,
  input  ENABLE,
  input  RESET,
  output R3,
  output R2,
  output R1,
  output R0
);

  wire j_k_ff_1_qn, j_k_ff_2_qn, j_k_ff_3_qn, not_1_out;

  not not_1 (not_1_out, in_1);
  J_K_Flip_Flop j_k_ff_1 (
    .J(in_1), .clk(CLK), .K(not_1_out), .Q(R3), .Qn(j_k_ff_1_qn), .preset(PERSET), .en(ENABLE), .reset(RESET));
  J_K_Flip_Flop j_k_ff_2 (
    .J(R3), .clk(CLK), .K(j_k_ff_1_qn), .Q(R2), .Qn(j_k_ff_2_qn), .preset(PERSET), .en(ENABLE), .reset(RESET));
  J_K_Flip_Flop j_k_ff_3 (
    .J(R2), .clk(CLK), .K(j_k_ff_2_qn), .Q(R1), .Qn(j_k_ff_3_qn), .preset(PERSET), .en(ENABLE), .reset(RESET));
  J_K_Flip_Flop j_k_ff_4 (
    .J(R1), .clk(CLK), .K(j_k_ff_3_qn), .Q(R0), .preset(PERSET), .en(ENABLE), .reset(RESET));  // open: Qn
endmodule
