// Logisim project case-1.circ as structural Verilog: 1 circuit, main circuit main
module main (
  input  [1:0] in_1,
  input  A0,
  input  B0,
  input  A1,
  input  B1,
  input  A2,
  input  B2,
  input  A3,
  input  B3,
  input  in_10,
  input  Cin,
  output out_12,
  output out_13,
  output out_14,
  output out_15,
  output out_16,
  output out_17,
  output out_18,
  output out_19,
  output out_20
);

  wire and_1_out, and_2_out, and_3_out, and_4_out, main_1_co, main_1_s, main_2_s, main_3_co, main_3_s,
       main_4_co, main_4_s, multiplexer_1_out, multiplexer_2_out, multiplexer_3_out, multiplexer_4_out,
       multiplexer_5_out, multiplexer_6_out, multiplexer_7_out, multiplexer_8_out, not_1_out, not_2_out,
       not_3_out, not_4_out, not_5_out, not_6_out, not_7_out, not_8_out, not_9_out, or_1_out, or_2_out,
       or_3_out, or_4_out, xor_1_out, xor_2_out, xor_3_out, xor_4_out;

  not not_1 (not_1_out, 1'b0);
  and and_1 (and_1_out, A0, B0);
  or or_1 (or_1_out, A0, B0);
  xor xor_1 (xor_1_out, A0, B0);
  not not_2 (not_2_out, A0);
  and and_2 (and_2_out, A1, B1);
  or or_2 (or_2_out, A1, B1);
  xor xor_2 (xor_2_out, A1, B1);
  not not_3 (not_3_out, A1);
  and and_3 (and_3_out, A2, B2);
  or or_3 (or_3_out, A2, B2);
  xor xor_3 (xor_3_out, A2, B2);
  not not_4 (not_4_out, A2);
  and and_4 (and_4_out, A3, B3);
  or or_4 (or_4_out, A3, B3);
  xor xor_4 (xor_4_out, A3, B3);
  not not_5 (not_5_out, A3);
  not not_6 (not_6_out, B0);
  Multiplexer #(.select(2), .enable("false")) multiplexer_1 (
    .in0(B0), .in1(not_6_out), .in2(not_1_out), .out(multiplexer_1_out), .sel(in_1));  // open: in3
  not not_7 (not_7_out, B1);
  Multiplexer #(.select(2), .enable("false")) multiplexer_2 (
    .in0(B1), .in1(not_7_out), .in2(not_1_out), .in3(1'b0), .out(multiplexer_2_out), .sel(in_1));
  not not_8 (not_8_out, B2);
  Multiplexer #(.select(2), .enable("false")) multiplexer_3 (
    .in0(B2), .in1(not_8_out), .in2(not_1_out), .in3(1'b0), .out(multiplexer_3_out), .sel(in_1));
  not not_9 (not_9_out, B3);
  Multiplexer #(.select(2), .enable("false")) multiplexer_4 (
    .in0(B3), .in1(not_9_out), .in2(not_1_out), .in3(1'b0), .out(multiplexer_4_out), .sel(in_1));
  Multiplexer #(.select(2), .enable("false")) multiplexer_5 (
    .in0(and_1_out), .in1(or_1_out), .in2(xor_1_out), .in3(not_2_out), .out(multiplexer_5_out), .sel(in_1));
  Multiplexer #(.select(2), .enable("false")) multiplexer_6 (
    .in0(and_2_out), .in1(or_2_out), .in2(xor_2_out), .in3(not_3_out), .out(multiplexer_6_out), .sel(in_1));
  Multiplexer #(.select(2), .enable("false")) multiplexer_7 (
    .in0(and_3_out), .in1(or_3_out), .in2(xor_3_out), .in3(not_4_out), .out(multiplexer_7_out), .sel(in_1));
  Multiplexer #(.select(2), .enable("false")) multiplexer_8 (
    .in0(and_4_out), .in1(or_4_out), .in2(xor_4_out), .in3(not_5_out), .out(multiplexer_8_out), .sel(in_1));
  FA_main main_1 (.A(A0), .B(multiplexer_1_out), .Cin(out_14), .S(main_1_s), .Co(main_1_co));
  FA_main main_2 (.A(A1), .B(multiplexer_2_out), .Cin(main_3_co), .S(main_2_s), .Co(out_14));
  FA_main main_3 (.A(A2), .B(multiplexer_3_out), .Cin(main_4_co), .S(main_3_s), .Co(main_3_co));
  FA_main main_4 (.A(A3), .B(multiplexer_4_out), .Cin(Cin), .S(main_4_s), .Co(main_4_co));
  Multiplexer #(.enable("false")) multiplexer_9 (.in0(main_1_s), .in1(1'b0), .out(out_16), .sel(in_10));
  Multiplexer #(.enable("false")) multiplexer_10 (.in0(main_1_co), .in1(multiplexer_5_out), .out(out_12), .sel(in_10));
  Multiplexer #(.enable("false")) multiplexer_11 (.in0(main_2_s), .in1(multiplexer_6_out), .out(out_18), .sel(in_10));
  Multiplexer #(.enable("false")) multiplexer_12 (.in0(main_3_s), .in1(multiplexer_7_out), .out(out_19), .sel(in_10));
  Multiplexer #(.enable("false")) multiplexer_13 (.in0(main_4_s), .in1(multiplexer_8_out), .out(out_20), .sel(in_10));
  xor xor_5 (out_15, out_14, main_1_s);
  ExactlyOne xor_6 (.out(out_13), .in0(out_12), .in1(out_18), .in2(out_19), .in3(out_20));

  assign out_17 = out_12;
endmodule
