// Logisim project 1 bit memory cell.circ as structural Verilog: 1 circuit, main circuit main
module main (
  input  SEL,
  input  D_IN,
  input  CLK,
  input  R_W_BAR,
  output D_OUT
);

  wire and_1_out, and_2_out, main_1_q, not_1_out, not_2_out;

  not not_1 (not_1_out, D_IN);
  not not_2 (not_2_out, R_W_BAR);
  and and_1 (and_1_out, SEL, SEL, D_IN, CLK);
  and and_2 (and_2_out, CLK, not_1_out, SEL, not_2_out);
  SR_flip_flop_main main_1 (.S(and_1_out), .R(and_2_out), .Q(main_1_q));  // open: Q_BAR
  and and_3 (D_OUT, SEL, main_1_q, R_W_BAR);
endmodule
