// Logisim project 2 to 4 decoder.circ as structural Verilog: 1 circuit, main circuit main
module main (
  input  CS,
  input  B,
  input  A,
  output A3,
  output A2,
  output A1,
  output Q0
);

  wire not_1_out, not_2_out, not_3_out;

  not not_1 (not_1_out, CS);
  not not_2 (not_2_out, B);
  not not_3 (not_3_out, A);
  and AND3 (A3, not_1_out, B, A);
  and AND2 (A2, not_1_out, B, not_3_out);
  and AND1 (A1, not_1_out, not_2_out, A);
  and AND0 (Q0, not_3_out, not_2_out, not_1_out);
endmodule
