// Logisim project SR flip flop.circ as structural Verilog: 1 circuit, main circuit main
module main (
  input  S,
  input  R,
  output Q_BAR,
  output Q
);

  nor NOR0 (Q_BAR, S, Q);
  nor NOR1 (Q, Q_BAR, R);
endmodule
