// Logisim project 8-Bit ALU CIRCUIT.circ as structural Verilog: 1 circuit, main circuit main
module main (
  input  [1:0] in_1,
  input  A7,
  input  B7,
  input  A6,
  input  B6,
  input  A5,
  input  B5,
  input  A4,
  input  B4,
  input  A3,
  input  B3,
  input  A2,
  input  B2,
  input  A1,
  input  B1,
  input  A0,
  input  B0,
  input  in_18,
  input  CIN,
  output S,
  output C,
  output V,
  output Z,
  output S8,
  output S7,
  output S6,
  output S5,
  output S4,
  output S3,
  output S2,
  output S1,
  output S0
);

  wire AND_2_out, AND_3_out, AND_4_out, AND_5_out, AND_6_out, AND_7_out, AND_8_out, AND_out, main_1_out_4,
       main_1_out_5, main_2_out_4, main_3_out_4, main_3_out_5, main_4_out_4, main_4_out_5, main_5_out_4,
       main_5_out_5, main_6_out_4, main_6_out_5, main_7_out_4, main_7_out_5, main_8_out_4, main_8_out_5,
       multiplexer_1_out, multiplexer_2_out, multiplexer_3_out, multiplexer_4_out, multiplexer_5_out,
       multiplexer_6_out, multiplexer_7_out, multiplexer_8_out, multiplexer_9_out, multiplexer_10_out,
       multiplexer_11_out, multiplexer_12_out, multiplexer_13_out, multiplexer_14_out, multiplexer_15_out,
       multiplexer_16_out, not_1_out, not_2_out, not_3_out, not_4_out, not_5_out, not_6_out, not_7_out,
       not_8_out, not_9_out, not_10_out, not_11_out, not_12_out, not_13_out, not_14_out, not_15_out,
       not_16_out, not_17_out, OR_2_out, OR_3_out, OR_4_out, OR_5_out, OR_6_out, OR_7_out, OR_8_out, OR_out,
       XOR_2_out, XOR_3_out, XOR_4_out, XOR_5_out, XOR_6_out, XOR_7_out, XOR_8_out, XOR_out;

  not not_1 (not_1_out, 1'b0);
  not not_2 (not_2_out, B7);
  Multiplexer #(.select(2), .enable("false")) multiplexer_1 (
    .in0(B7), .in1(not_2_out), .in2(not_1_out), .in3(1'b0), .out(multiplexer_1_out), .sel(in_1));
  not not_3 (not_3_out, B6);
  Multiplexer #(.select(2), .enable("false")) multiplexer_2 (
    .in0(B6), .in1(not_3_out), .in2(not_1_out), .in3(1'b0), .out(multiplexer_2_out), .sel(in_1));
  not not_4 (not_4_out, B5);
  Multiplexer #(.select(2), .enable("false")) multiplexer_3 (
    .in0(B5), .in1(not_4_out), .in2(not_1_out), .in3(1'b0), .out(multiplexer_3_out), .sel(in_1));
  not not_5 (not_5_out, B4);
  Multiplexer #(.select(2), .enable("false")) multiplexer_4 (
    .in0(B4), .in1(not_5_out), .in2(not_1_out), .in3(1'b0), .out(multiplexer_4_out), .sel(in_1));
  not not_6 (not_6_out, B3);
  Multiplexer #(.select(2), .enable("false")) multiplexer_5 (
    .in0(B3), .in1(not_6_out), .in2(not_1_out), .in3(1'b0), .out(multiplexer_5_out), .sel(in_1));
  not not_7 (not_7_out, B2);
  Multiplexer #(.select(2), .enable("false")) multiplexer_6 (
    .in0(B2), .in1(not_7_out), .in2(not_1_out), .in3(1'b0), .out(multiplexer_6_out), .sel(in_1));
  not not_8 (not_8_out, B1);
  Multiplexer #(.select(2), .enable("false")) multiplexer_7 (
    .in0(B1), .in1(not_8_out), .in2(not_1_out), .in3(1'b0), .out(multiplexer_7_out), .sel(in_1));
  not not_9 (not_9_out, B0);
  Multiplexer #(.select(2), .enable("false")) multiplexer_8 (
    .in0(B0), .in1(not_9_out), .in2(not_1_out), .in3(1'b0), .out(multiplexer_8_out), .sel(in_1));
  and AND (AND_out, A7, B7);
  or OR (OR_out, A7, B7);
  xor XOR (XOR_out, A7, B7);
  not not_10 (not_10_out, A7);
  and AND_2 (AND_2_out, A6, B6);
  or OR_2 (OR_2_out, A6, B6);
  xor XOR_2 (XOR_2_out, A6, B6);
  not not_11 (not_11_out, A6);
  and AND_3 (AND_3_out, A5, B5);
  or OR_3 (OR_3_out, A5, B5);
  xor XOR_3 (XOR_3_out, A5, B5);
  not not_12 (not_12_out, A5);
  and AND_4 (AND_4_out, A4, B4);
  or OR_4 (OR_4_out, A4, B4);
  xor XOR_4 (XOR_4_out, A4, B4);
  not not_13 (not_13_out, A4);
  and AND_5 (AND_5_out, A3, B3);
  or OR_5 (OR_5_out, A3, B3);
  xor XOR_5 (XOR_5_out, A3, B3);
  not not_14 (not_14_out, A3);
  and AND_6 (AND_6_out, A2, B2);
  or OR_6 (OR_6_out, A2, B2);
  xor XOR_6 (XOR_6_out, A2, B2);
  not not_15 (not_15_out, A2);
  and AND_7 (AND_7_out, A1, B1);
  or OR_7 (OR_7_out, A1, B1);
  xor XOR_7 (XOR_7_out, A1, B1);
  not not_16 (not_16_out, A1);
  and AND_8 (AND_8_out, A0, B0);
  or OR_8 (OR_8_out, A0, B0);
  xor XOR_8 (XOR_8_out, A0, B0);
  not not_17 (not_17_out, A0);
  Multiplexer #(.select(2), .enable("false")) multiplexer_9 (
    .in0(AND_out), .in1(OR_out), .in2(XOR_out), .in3(not_10_out), .out(multiplexer_9_out), .sel(in_1));
  Multiplexer #(.select(2), .enable("false")) multiplexer_10 (
    .in0(AND_2_out), .in1(OR_2_out), .in2(XOR_2_out), .in3(not_11_out), .out(multiplexer_10_out), .sel(in_1));
  Multiplexer #(.select(2), .enable("false")) multiplexer_11 (
    .in0(AND_3_out), .in1(OR_3_out), .in2(XOR_3_out), .in3(not_12_out), .out(multiplexer_11_out), .sel(in_1));
  Multiplexer #(.select(2), .enable("false")) multiplexer_12 (
    .in0(AND_4_out), .in1(OR_4_out), .in2(XOR_4_out), .in3(not_13_out), .out(multiplexer_12_out), .sel(in_1));
  Multiplexer #(.select(2), .enable("false")) multiplexer_13 (
    .in0(AND_5_out), .in1(OR_5_out), .in2(XOR_5_out), .in3(not_14_out), .out(multiplexer_13_out), .sel(in_1));
  Multiplexer #(.select(2), .enable("false")) multiplexer_14 (
    .in0(AND_6_out), .in1(OR_6_out), .in2(XOR_6_out), .in3(not_15_out), .out(multiplexer_14_out), .sel(in_1));
  Multiplexer #(.select(2), .enable("false")) multiplexer_15 (
    .in0(AND_7_out), .in1(OR_7_out), .in2(XOR_7_out), .in3(not_16_out), .out(multiplexer_15_out), .sel(in_1));
  Multiplexer #(.select(2), .enable("false")) multiplexer_16 (
    .in0(AND_8_out), .in1(OR_8_out), .in2(XOR_8_out), .in3(not_17_out), .out(multiplexer_16_out), .sel(in_1));
  full_adder_main main_1 (.in_1(A7), .in_2(multiplexer_1_out), .in_3(C), .out_4(main_1_out_4), .out_5(main_1_out_5));
  full_adder_main main_2 (.in_1(A6), .in_2(multiplexer_2_out), .in_3(main_3_out_5), .out_4(main_2_out_4), .out_5(C));
  full_adder_main main_3 (
    .in_1(A5), .in_2(multiplexer_3_out), .in_3(main_4_out_5), .out_4(main_3_out_4), .out_5(main_3_out_5));
  full_adder_main main_4 (
    .in_1(A4), .in_2(multiplexer_4_out), .in_3(main_5_out_5), .out_4(main_4_out_4), .out_5(main_4_out_5));
  full_adder_main main_5 (
    .in_1(A3), .in_2(multiplexer_5_out), .in_3(main_6_out_5), .out_4(main_5_out_4), .out_5(main_5_out_5));
  full_adder_main main_6 (
    .in_1(A2), .in_2(multiplexer_6_out), .in_3(main_7_out_5), .out_4(main_6_out_4), .out_5(main_6_out_5));
  full_adder_main main_7 (
    .in_1(A1), .in_2(multiplexer_7_out), .in_3(main_8_out_5), .out_4(main_7_out_4), .out_5(main_7_out_5));
  full_adder_main main_8 (.in_1(A0), .in_2(multiplexer_8_out), .in_3(CIN), .out_4(main_8_out_4), .out_5(main_8_out_5));
  Multiplexer #(.enable("false")) multiplexer_17 (.in0(main_1_out_5), .in1(1'b0), .out(S), .sel(in_18));
  Multiplexer #(.enable("false")) multiplexer_18 (.in0(main_1_out_4), .in1(multiplexer_9_out), .out(S7), .sel(in_18));
  Multiplexer #(.enable("false")) multiplexer_19 (.in0(main_2_out_4), .in1(multiplexer_10_out), .out(S6), .sel(in_18));
  Multiplexer #(.enable("false")) multiplexer_20 (.in0(main_3_out_4), .in1(multiplexer_11_out), .out(S5), .sel(in_18));
  Multiplexer #(.enable("false")) multiplexer_21 (.in0(main_4_out_4), .in1(multiplexer_12_out), .out(S4), .sel(in_18));
  Multiplexer #(.enable("false")) multiplexer_22 (.in0(main_5_out_4), .in1(multiplexer_13_out), .out(S3), .sel(in_18));
  Multiplexer #(.enable("false")) multiplexer_23 (.in0(main_6_out_4), .in1(multiplexer_14_out), .out(S2), .sel(in_18));
  Multiplexer #(.enable("false")) multiplexer_24 (.in0(main_7_out_4), .in1(multiplexer_15_out), .out(S1), .sel(in_18));
  Multiplexer #(.enable("false")) multiplexer_25 (.in0(main_8_out_4), .in1(multiplexer_16_out), .out(S0), .sel(in_18));
  xor XOR_9 (V, C, main_1_out_5);
  ExactlyOne XOR_10 (.out(Z), .in0(S), .in1(S7), .in2(S6), .in3(S5), .in4(S4), .in5(S3), .in6(S2), .in7(S1), .in8(S0));

  assign S8 = S;

  // Notes on the sheet:
  //   8-Bit ALU Circuit
endmodule
